# Fritzing sketch CrocoMeca (saved by Fritzing 0.9.3b)
breadboards: 1

parts:
  Composant1 = Arduino Uno (Rev3)
  Composant2 = SRF05 Ultrasonic Rangefinder
  J1 = Basic Servo

nets:
  N1: Composant1.D8, Composant2.Echo
  N2: Composant1.D9_PWM, Composant2.Trig
  N3: Composant1.D2, J1.pulse
  VCC: Composant1.5V, Composant2.VCC, J1.vcc
  GND: Composant1.GND, Composant2.GND, J1.gnd
